# Fritzing sketch audiopot (saved by Fritzing 0.9.4)

parts:
  Part1 = Arduino Nano (Rev3.0) (ICSP)
  RE1 = KY-040 Rotary encoder [package=THT]
  X1 = USB Connectors [package=usb-a-h]
  R1 = Resistor [tolerance=±5% power=0.25 resistance=100 package=THT]
  R2 = Resistor [tolerance=±5% power=0.25 resistance=100 package=THT]
  R3 = Resistor [tolerance=±5% power=0.25 resistance=2.2k package=THT]
  0_47uF = Capacitor Polarized [package=cpol-radial-100uf-25v]
  0_47uF_2 = Capacitor Polarized [package=cpol-radial-100uf-25v]  # not connected

nets:
  N1: Part1.D2, R1.Pin_1
  N2: Part1.D4, R2.Pin_1
  N3: Part1.D5, R3.Pin_1
  N4: Part1.D9, RE1.CLK, 0_47uF.-
  N5: Part1.D10, RE1.DT
  N6: Part1.D11/MOSI, RE1.SW
  GND: Part1.GND, RE1.GND, X1.GND
  5V: Part1.5V, RE1.Vcc, X1.VBUS
  N7: X1.D-, R2.Pin_0
  N8: X1.D+, R1.Pin_0

custom parts:
  KY-040 Rotary encoder: KY-040 Rotary Encoder with switch on breakout borad from AZ Delivery
